# Fritzing sketch edison-coffee (saved by Fritzing 0.9.2b)
breadboards: 1

parts:
  U2 = EDISON  # not connected
  U3 = EDISON
  BC547 = NPN-Transistor [package="TO92 [THT]"]
  U5 = RELAY [package=relay-jzc]
  LED1 = LED - 5mm [color="Red (633nm)" package="5 mm [THT]"]
  Composant1 = Rectifier Diode [part_number=1N4148 package="300 mil [THT]"]
  BC548 = NPN-Transistor [package="TO92 [THT]"]
  Composant2 = Rectifier Diode [part_number=1N4148 package="300 mil [THT]"]

nets:
  N1: U3.NC, U5.COIL2, LED1.cathode
  N2: U3.GP134, BC547.C, U5.NC, BC548.C
  N3: U3.GP49, Composant1.anode
  N4: U3.GP84, Composant2.anode
  N5: BC547.E, U5.NO
  N6: BC547.B, Composant1.cathode
  N7: LED1.anode, BC548.E
  N8: BC548.B, Composant2.cathode

custom parts:
  Rectifier Diode: A standard rectifier diode
